// Logisim project MorrisMano_Computer.circ as structural Verilog: 23 circuits, main circuit main
module main (
  input  [15:0] in_1,
  input  in_2,
  input  [7:0] in_3,
  input  in_4,
  output [15:0] out_5,
  output [7:0] out_6,
  output [15:0] out_7,
  output [15:0] out_8,
  output [3:0] out_9,
  output [15:0] out_10,
  output [15:0] out_11,
  output out_12,
  output [7:0] out_13,
  output [15:0] out_14,
  output [15:0] out_15,
  output [7:0] out_16
);

  wire ac_controller_1_ac_clr, ac_controller_1_ac_ld, ar_controller_1_ar_clr, ar_controller_1_ar_inr,
       ar_controller_1_ar_ld, bus_8x3_encoder_1_s0, bus_8x3_encoder_1_s1, bus_8x3_encoder_1_s2,
       bus_controller_1_x1, bus_controller_1_x2, bus_controller_1_x3, bus_controller_1_x4,
       bus_controller_1_x5, bus_controller_1_x6, bus_controller_1_x7, CLK, dr_controller_1_dr_inr,
       dr_controller_1_dr_ld, E, E_ALU, ff_controller_1_clke, ff_controller_1_clkfgi, ff_controller_1_clkfgo,
       ff_controller_1_clki, ff_controller_1_clkien, ff_controller_1_clkr, ff_controller_1_clks,
       ff_controller_1_eclr, ff_controller_1_eset, ff_controller_1_fgiclr, ff_controller_1_fgoclr,
       ff_controller_1_ienclr, ff_controller_1_ienset, ff_controller_1_iset, ff_controller_1_rclr,
       ff_controller_1_rset, ff_controller_1_sclr, ff_controller_1_sset, FGI, FGO, I, IEN,
       ir_controller_1_ir_ld, outr_controller_1_outr_ld, pc_controller_1_pc_clr, pc_controller_1_pc_inr,
       pc_controller_1_pc_ld, R, ram_controller_1_read, ram_controller_1_write, S,
       sc_controller_clr_1_sc_clr_out, tr_controller_1_tr_ld;
  wire [11:0] ram_adjuster_1_ram_output_out;
  wire [15:0] ALU_OUT, RAM_mem, TR;

  Clock clock_1 (.out(CLK));
  SC_CONTROLLER_CLR sc_controller_clr_1 (
    .IR(out_14), .Timer(out_9), .R(R), .SC_CLR_OUT(sc_controller_clr_1_sc_clr_out));
  COUNTER4BIT counter4bit_1 (.INR(S), .CLK(CLK), .CLR(sc_controller_clr_1_sc_clr_out), .O(out_9));
  ALU alu_1 (
    .E(E), .AC(out_7), .DR(out_8), .INPR(out_13), .Timer(out_9), .IR(out_14), .ALU_OUTPUT(ALU_OUT),
    .ExtendBit(E_ALU));
  RAM_CONTROLLER ram_controller_1 (
    .Timer(out_9), .R(R), .IR(out_14), .Read(ram_controller_1_read), .Write(ram_controller_1_write));
  RAM #(.addrWidth(12), .asyncread("true"), .dataWidth(16)) ram_1 (
    .addr(ram_adjuster_1_ram_output_out), .we(ram_controller_1_write), .oe(ram_controller_1_read), .clk(CLK),
    .din(out_15), .dout(RAM_mem));
  RAM_ADJUSTER ram_adjuster_1 (.RAM_INPUT_IN(out_10), .RAM_OUTPUT_OUT(ram_adjuster_1_ram_output_out));
  AR_CONTROLLER ar_controller_1 (
    .IR(out_14), .Timer(out_9), .R(R), .AR_LD(ar_controller_1_ar_ld), .AR_INR(ar_controller_1_ar_inr),
    .AR_CLR(ar_controller_1_ar_clr));
  PC_CONTROLLER pc_controller_1 (
    .E(E), .FGI(FGI), .FGO(FGO), .IR(out_14), .Timer(out_9), .R(R), .AC(out_7), .DR(out_8),
    .PC_LD(pc_controller_1_pc_ld), .PC_CLR(pc_controller_1_pc_clr), .PC_INR(pc_controller_1_pc_inr));
  DR_CONTROLLER dr_controller_1 (
    .IR(out_14), .Timer(out_9), .DR_LD(dr_controller_1_dr_ld), .DR_INR(dr_controller_1_dr_inr));
  AC_CONTROLLER ac_controller_1 (
    .IR(out_14), .Timer(out_9), .AC_INR(out_12), .AC_CLR(ac_controller_1_ac_clr),
    .AC_LD(ac_controller_1_ac_ld));
  INPR inpr_1 (.D(in_3), .O(out_13));
  IR_CONTROLLER ir_controller_1 (.Timer(out_9), .R(R), .IR_LD(ir_controller_1_ir_ld));
  TR_CONTROLLER tr_controller_1 (.Timer(out_9), .R(R), .TR_LD(tr_controller_1_tr_ld));
  OUTR_CONTROLLER outr_controller_1 (.IR(out_14), .Timer(out_9), .OUTR_LD(outr_controller_1_outr_ld));
  RAM_BLOCK ram_block_1 ();  // open: Address_Input, Write, CLK, Read, Data_Input, O
  REGISTER12BIT AR (
    .LD(ar_controller_1_ar_ld), .INC(ar_controller_1_ar_inr), .D(out_15), .CLR(ar_controller_1_ar_clr),
    .CLK(CLK), .O(out_10));
  REGISTER12BIT PC (
    .LD(pc_controller_1_pc_ld), .INC(pc_controller_1_pc_inr), .D(out_15), .CLR(pc_controller_1_pc_clr),
    .CLK(CLK), .O(out_11));
  REGISTER16BIT DR (
    .D(out_15), .LD(dr_controller_1_dr_ld), .INC(dr_controller_1_dr_inr), .CLK(CLK), .O(out_8));  // open: CLR
  REGISTER16BIT AC (
    .D(ALU_OUT), .LD(ac_controller_1_ac_ld), .INC(out_12), .CLR(ac_controller_1_ac_clr), .CLK(CLK), .O(out_7));
  REGISTER16BIT IR (.D(out_15), .LD(ir_controller_1_ir_ld), .CLK(CLK), .O(out_14));  // open: INC, CLR
  REGISTER16BIT u_TR (.D(out_15), .LD(tr_controller_1_tr_ld), .CLK(CLK), .O(TR));  // open: INC, CLR
  OUTR outr_1 (.CLK(CLK), .LD(outr_controller_1_outr_ld), .D(out_15), .O(out_6));  // open: CLR
  BUS_8x3_ENCODER bus_8x3_encoder_1 (
    .x1(bus_controller_1_x1), .x2(bus_controller_1_x2), .x3(bus_controller_1_x3), .x4(bus_controller_1_x4),
    .x5(bus_controller_1_x5), .x6(bus_controller_1_x6), .x7(bus_controller_1_x7), .S0(bus_8x3_encoder_1_s0),
    .S1(bus_8x3_encoder_1_s1), .S2(bus_8x3_encoder_1_s2));
  BUS_CONTROLLER bus_controller_1 (
    .IR(out_14), .Timer(out_9), .R(R), .x7(bus_controller_1_x7), .x2(bus_controller_1_x2),
    .x3(bus_controller_1_x3), .x4(bus_controller_1_x4), .x5(bus_controller_1_x5), .x1(bus_controller_1_x1),
    .x6(bus_controller_1_x6));
  J_K_Flip_Flop u_E (
    .J(ff_controller_1_eset), .K(ff_controller_1_eclr), .clk(ff_controller_1_clke), .Q(E));  // open: Qn, preset, reset
  J_K_Flip_Flop u_I (.J(ff_controller_1_iset), .clk(ff_controller_1_clki), .Q(I));  // open: K, Qn, preset, reset
  FF_CONTROLLER ff_controller_1 (
    .alu_E(E_ALU), .START(in_4), .IR(out_14), .CLK(CLK), .FGO(FGO), .Timer(out_9), .R(R), .IEN(IEN),
    .FGI(FGI), .Eclr(ff_controller_1_eclr), .Eset(ff_controller_1_eset), .FGOclr(ff_controller_1_fgoclr),
    .Iset(ff_controller_1_iset), .Sset(ff_controller_1_sset), .Sclr(ff_controller_1_sclr),
    .Rset(ff_controller_1_rset), .Rclr(ff_controller_1_rclr), .IENset(ff_controller_1_ienset),
    .IENclr(ff_controller_1_ienclr), .FGIclr(ff_controller_1_fgiclr), .CLKI(ff_controller_1_clki),
    .CLKS(ff_controller_1_clks), .CLKR(ff_controller_1_clkr), .CLKIEN(ff_controller_1_clkien),
    .CLKFGI(ff_controller_1_clkfgi), .CLKFGO(ff_controller_1_clkfgo), .CLKE(ff_controller_1_clke));
  J_K_Flip_Flop u_S (
    .J(ff_controller_1_sset), .K(ff_controller_1_sclr), .clk(ff_controller_1_clks), .Q(S));  // open: Qn, preset, reset
  J_K_Flip_Flop u_R (
    .J(ff_controller_1_rset), .K(ff_controller_1_rclr), .clk(ff_controller_1_clkr), .Q(R));  // open: Qn, preset, reset
  J_K_Flip_Flop u_IEN (
    .J(ff_controller_1_ienset), .K(ff_controller_1_ienclr), .clk(ff_controller_1_clkien), .Q(IEN));  // open: Qn, preset, reset
  J_K_Flip_Flop u_FGI (
    .K(ff_controller_1_fgiclr), .clk(ff_controller_1_clkfgi), .Q(FGI));  // open: J, Qn, preset, reset
  J_K_Flip_Flop u_FGO (
    .K(ff_controller_1_fgoclr), .clk(ff_controller_1_clkfgo), .Q(FGO));  // open: J, Qn, preset, reset
  BUS_BLOCK bus_block_1 (
    .AR(out_10), .PC(out_11), .DR(out_8), .AC(out_7), .IR(out_14), .TR(TR), .MEM(RAM_mem),
    .S0(bus_8x3_encoder_1_s0), .S1(bus_8x3_encoder_1_s1), .S2(bus_8x3_encoder_1_s2), .O(out_15));

  assign out_5 = in_1;
  assign out_16 = out_6;

  // Other names for the same wires on the sheet: AC[15:0] = out_7; AR[15:0] = out_10; BUS_OUT[15:0] = out_15;
  //   DR[15:0] = out_8; INPR_OUT[7:0] = out_13; IR[15:0] = out_14; OUTR_OUT[7:0] = out_6; PC[15:0] = out_11;
  //   SC[3:0] = out_9
endmodule

module BUS_BLOCK (
  input  [15:0] AR,
  input  [15:0] PC,
  input  [15:0] DR,
  input  [15:0] AC,
  input  [15:0] IR,
  input  [15:0] TR,
  input  [15:0] MEM,
  input  S0,
  input  S1,
  input  S2,
  output [15:0] O
);

  Multiplexer #(.select(3), .width(16)) multiplexer_1 (
    .in1(AR), .in2(PC), .in3(DR), .in4(AC), .in5(IR), .in6(TR), .in7(MEM), .out(O), .sel({S2, S1, S0}));  // open: in0
endmodule

module RAM_BLOCK (
  input  [15:0] Data_Input,
  input  Write,
  input  CLK,
  input  Read,
  input  [11:0] Address_Input,
  output [15:0] O
);

  wire WE_0, WE_1, WE_2, WE_3, WE_4, WE_5, WE_6, WE_7, WE_8, WE_9, WE_10, WE_11, WE_12, WE_13, WE_14, WE_15,
       WE_16, WE_17, WE_18, WE_19, WE_20, WE_21, WE_22, WE_23, WE_24, WE_25, WE_26, WE_27, WE_28, WE_29,
       WE_30, WE_31;
  wire [15:0] D_W_0, D_W_1, D_W_2, D_W_3, D_W_4, D_W_5, D_W_6, D_W_7, D_W_8, D_W_9, D_W_10, D_W_11, D_W_12,
       D_W_13, D_W_14, D_W_15, D_W_16, D_W_17, D_W_18, D_W_19, D_W_20, D_W_21, D_W_22, D_W_23, D_W_24,
       D_W_25, D_W_26, D_W_27, D_W_28, D_W_29, D_W_30, D_W_31, multiplexer_1_out, Q_W_0, Q_W_1, Q_W_2, Q_W_3,
       Q_W_4, Q_W_5, Q_W_6, Q_W_7, Q_W_8, Q_W_9, Q_W_10, Q_W_11, Q_W_12, Q_W_13, Q_W_14, Q_W_15, Q_W_16,
       Q_W_17, Q_W_18, Q_W_19, Q_W_20, Q_W_21, Q_W_22, Q_W_23, Q_W_24, Q_W_25, Q_W_26, Q_W_27, Q_W_28,
       Q_W_29, Q_W_30, Q_W_31;

  Demultiplexer #(.select(5), .width(16)) demultiplexer_1 (
    .out0(D_W_0), .out1(D_W_1), .out2(D_W_2), .out3(D_W_3), .out4(D_W_4), .out5(D_W_5), .out6(D_W_6),
    .out7(D_W_7), .out8(D_W_8), .out9(D_W_9), .out10(D_W_10), .out11(D_W_11), .out12(D_W_12), .out13(D_W_13),
    .out14(D_W_14), .out15(D_W_15), .out16(D_W_16), .out17(D_W_17), .out18(D_W_18), .out19(D_W_19),
    .out20(D_W_20), .out21(D_W_21), .out22(D_W_22), .out23(D_W_23), .out24(D_W_24), .out25(D_W_25),
    .out26(D_W_26), .out27(D_W_27), .out28(D_W_28), .out29(D_W_29), .out30(D_W_30), .out31(D_W_31),
    .in(Data_Input), .sel(Address_Input[4:0]));
  Decoder #(.select(5)) decoder_1 (
    .out0(WE_0), .out1(WE_1), .out2(WE_2), .out3(WE_3), .out4(WE_4), .out5(WE_5), .out6(WE_6), .out7(WE_7),
    .out8(WE_8), .out9(WE_9), .out10(WE_10), .out11(WE_11), .out12(WE_12), .out13(WE_13), .out14(WE_14),
    .out15(WE_15), .out16(WE_16), .out17(WE_17), .out18(WE_18), .out19(WE_19), .out20(WE_20), .out21(WE_21),
    .out22(WE_22), .out23(WE_23), .out24(WE_24), .out25(WE_25), .out26(WE_26), .out27(WE_27), .out28(WE_28),
    .out29(WE_29), .out30(WE_30), .out31(WE_31), .sel(Address_Input[4:0]), .en(Write));
  MEM_Reg mem_reg_1 (.WE(WE_0), .CLK(CLK), .D(D_W_0), .O(Q_W_0));  // open: R
  MEM_Reg mem_reg_2 (.WE(WE_4), .CLK(CLK), .D(D_W_4), .O(Q_W_4));  // open: R
  MEM_Reg mem_reg_3 (.WE(WE_8), .CLK(CLK), .D(D_W_8), .O(Q_W_8));  // open: R
  MEM_Reg mem_reg_4 (.WE(WE_12), .CLK(CLK), .D(D_W_12), .O(Q_W_12));  // open: R
  MEM_Reg mem_reg_5 (.WE(WE_16), .CLK(CLK), .D(D_W_16), .O(Q_W_16));  // open: R
  MEM_Reg mem_reg_6 (.WE(WE_20), .CLK(CLK), .D(D_W_20), .O(Q_W_20));  // open: R
  MEM_Reg mem_reg_7 (.WE(WE_24), .CLK(CLK), .D(D_W_24), .O(Q_W_24));  // open: R
  MEM_Reg mem_reg_8 (.WE(WE_28), .CLK(CLK), .D(D_W_28), .O(Q_W_28));  // open: R
  MEM_Reg mem_reg_9 (.WE(WE_1), .CLK(CLK), .D(D_W_1), .O(Q_W_1));  // open: R
  MEM_Reg mem_reg_10 (.WE(WE_5), .CLK(CLK), .D(D_W_5), .O(Q_W_5));  // open: R
  MEM_Reg mem_reg_11 (.WE(WE_9), .CLK(CLK), .D(D_W_9), .O(Q_W_9));  // open: R
  MEM_Reg mem_reg_12 (.WE(WE_13), .CLK(CLK), .D(D_W_13), .O(Q_W_13));  // open: R
  MEM_Reg mem_reg_13 (.WE(WE_17), .CLK(CLK), .D(D_W_17), .O(Q_W_17));  // open: R
  MEM_Reg mem_reg_14 (.WE(WE_21), .CLK(CLK), .D(D_W_21), .O(Q_W_21));  // open: R
  MEM_Reg mem_reg_15 (.WE(WE_25), .CLK(CLK), .D(D_W_25), .O(Q_W_25));  // open: R
  MEM_Reg mem_reg_16 (.WE(WE_29), .CLK(CLK), .D(D_W_29), .O(Q_W_29));  // open: R
  MEM_Reg mem_reg_17 (.WE(Read), .CLK(CLK), .D(multiplexer_1_out), .O(O));  // open: R
  MEM_Reg mem_reg_18 (.WE(WE_2), .CLK(CLK), .D(D_W_2), .O(Q_W_2));  // open: R
  MEM_Reg mem_reg_19 (.WE(WE_6), .CLK(CLK), .D(D_W_6), .O(Q_W_6));  // open: R
  MEM_Reg mem_reg_20 (.WE(WE_10), .CLK(CLK), .D(D_W_10), .O(Q_W_10));  // open: R
  MEM_Reg mem_reg_21 (.WE(WE_14), .CLK(CLK), .D(D_W_14), .O(Q_W_14));  // open: R
  MEM_Reg mem_reg_22 (.WE(WE_18), .CLK(CLK), .D(D_W_18), .O(Q_W_18));  // open: R
  MEM_Reg mem_reg_23 (.WE(WE_22), .CLK(CLK), .D(D_W_22), .O(Q_W_22));  // open: R
  MEM_Reg mem_reg_24 (.WE(WE_26), .CLK(CLK), .D(D_W_26), .O(Q_W_26));  // open: R
  MEM_Reg mem_reg_25 (.WE(WE_30), .CLK(CLK), .D(D_W_30), .O(Q_W_30));  // open: R
  MEM_Reg mem_reg_26 (.WE(WE_3), .CLK(CLK), .D(D_W_3), .O(Q_W_3));  // open: R
  MEM_Reg mem_reg_27 (.WE(WE_7), .CLK(CLK), .D(D_W_7), .O(Q_W_7));  // open: R
  MEM_Reg mem_reg_28 (.WE(WE_11), .CLK(CLK), .D(D_W_11), .O(Q_W_11));  // open: R
  MEM_Reg mem_reg_29 (.WE(WE_15), .CLK(CLK), .D(D_W_15), .O(Q_W_15));  // open: R
  MEM_Reg mem_reg_30 (.WE(WE_19), .CLK(CLK), .D(D_W_19), .O(Q_W_19));  // open: R
  MEM_Reg mem_reg_31 (.WE(WE_23), .CLK(CLK), .D(D_W_23), .O(Q_W_23));  // open: R
  MEM_Reg mem_reg_32 (.WE(WE_27), .CLK(CLK), .D(D_W_27), .O(Q_W_27));  // open: R
  MEM_Reg mem_reg_33 (.WE(WE_31), .CLK(CLK), .D(D_W_31), .O(Q_W_31));  // open: R
  Multiplexer #(.select(5), .width(16)) multiplexer_1 (
    .in0(Q_W_0), .in1(Q_W_1), .in2(Q_W_2), .in3(Q_W_3), .in4(Q_W_4), .in5(Q_W_5), .in6(Q_W_6), .in7(Q_W_7),
    .in8(Q_W_8), .in9(Q_W_9), .in10(Q_W_10), .in11(Q_W_11), .in12(Q_W_12), .in13(Q_W_13), .in14(Q_W_14),
    .in15(Q_W_15), .in16(Q_W_16), .in17(Q_W_17), .in18(Q_W_18), .in19(Q_W_19), .in20(Q_W_20), .in21(Q_W_21),
    .in22(Q_W_22), .in23(Q_W_23), .in24(Q_W_24), .in25(Q_W_25), .in26(Q_W_26), .in27(Q_W_27), .in28(Q_W_28),
    .in29(Q_W_29), .in30(Q_W_30), .in31(Q_W_31), .out(multiplexer_1_out), .sel(Address_Input[4:0]));

  // Other names for the same wires on the sheet: RAM_Address_T[4:0] = Address_Input[4:0]; RAM_CLK_T = CLK;
  //   RAM_WRITE_T = Write
endmodule

module MEM_Reg (
  input  WE,
  input  CLK,
  input  [15:0] D,
  input  R,
  output [15:0] O
);

  wire and_1_out;

  and and_1 (and_1_out, WE, CLK);
  D_Flip_Flop d_ff_1 (.D(D[0]), .clk(and_1_out), .Q(O[0]), .reset(R));  // open: Qn, preset
  D_Flip_Flop d_ff_2 (.D(D[1]), .clk(and_1_out), .Q(O[1]), .reset(R));  // open: Qn, preset
  D_Flip_Flop d_ff_3 (.D(D[2]), .clk(and_1_out), .Q(O[2]), .reset(R));  // open: Qn, preset
  D_Flip_Flop d_ff_4 (.D(D[3]), .clk(and_1_out), .Q(O[3]), .reset(R));  // open: Qn, preset
  D_Flip_Flop d_ff_5 (.D(D[4]), .clk(and_1_out), .Q(O[4]), .reset(R));  // open: Qn, preset
  D_Flip_Flop d_ff_6 (.D(D[5]), .clk(and_1_out), .Q(O[5]), .reset(R));  // open: Qn, preset
  D_Flip_Flop d_ff_7 (.D(D[6]), .clk(and_1_out), .Q(O[6]), .reset(R));  // open: Qn, preset
  D_Flip_Flop d_ff_8 (.D(D[7]), .clk(and_1_out), .Q(O[7]), .reset(R));  // open: Qn, preset
  D_Flip_Flop d_ff_9 (.D(D[8]), .clk(and_1_out), .Q(O[8]), .reset(R));  // open: Qn, preset
  D_Flip_Flop d_ff_10 (.D(D[9]), .clk(and_1_out), .Q(O[9]), .reset(R));  // open: Qn, preset
  D_Flip_Flop d_ff_11 (.D(D[10]), .clk(and_1_out), .Q(O[10]), .reset(R));  // open: Qn, preset
  D_Flip_Flop d_ff_12 (.D(D[11]), .clk(and_1_out), .Q(O[11]), .reset(R));  // open: Qn, preset
  D_Flip_Flop d_ff_13 (.D(D[12]), .clk(and_1_out), .Q(O[12]), .reset(R));  // open: Qn, preset
  D_Flip_Flop d_ff_14 (.D(D[13]), .clk(and_1_out), .Q(O[13]), .reset(R));  // open: Qn, preset
  D_Flip_Flop d_ff_15 (.D(D[14]), .clk(and_1_out), .Q(O[14]), .reset(R));  // open: Qn, preset
  D_Flip_Flop d_ff_16 (.D(D[15]), .clk(and_1_out), .Q(O[15]), .reset(R));  // open: Qn, preset
endmodule

module REGISTER16BIT (
  input  LD,
  input  INC,
  input  CLR,
  input  CLK,
  input  [15:0] D,
  output [15:0] O
);

  wire and_1_out, not_1_out, SL1_16BIT;
  wire [15:0] adder_1_out, d_ff_1_q, multiplexer_1_out;

  Multiplexer #(.width(16)) multiplexer_1 (.in0(O), .in1(D), .out(multiplexer_1_out), .sel(LD));
  and and_1 (and_1_out, CLR, CLK);
  not not_1 (not_1_out, LD);
  and and_2 (SL1_16BIT, not_1_out, INC);
  D_Flip_Flop d_ff_1 (.D(multiplexer_1_out[0]), .clk(CLK), .Q(d_ff_1_q[0]), .reset(and_1_out));  // open: Qn, preset
  D_Flip_Flop d_ff_2 (.D(multiplexer_1_out[1]), .clk(CLK), .Q(d_ff_1_q[1]), .reset(and_1_out));  // open: Qn, preset
  D_Flip_Flop d_ff_3 (.D(multiplexer_1_out[2]), .clk(CLK), .Q(d_ff_1_q[2]), .reset(and_1_out));  // open: Qn, preset
  D_Flip_Flop d_ff_4 (.D(multiplexer_1_out[3]), .clk(CLK), .Q(d_ff_1_q[3]), .reset(and_1_out));  // open: Qn, preset
  D_Flip_Flop d_ff_5 (.D(multiplexer_1_out[4]), .clk(CLK), .Q(d_ff_1_q[4]), .reset(and_1_out));  // open: Qn, preset
  D_Flip_Flop d_ff_6 (.D(multiplexer_1_out[5]), .clk(CLK), .Q(d_ff_1_q[5]), .reset(and_1_out));  // open: Qn, preset
  D_Flip_Flop d_ff_7 (.D(multiplexer_1_out[6]), .clk(CLK), .Q(d_ff_1_q[6]), .reset(and_1_out));  // open: Qn, preset
  D_Flip_Flop d_ff_8 (.D(multiplexer_1_out[7]), .clk(CLK), .Q(d_ff_1_q[7]), .reset(and_1_out));  // open: Qn, preset
  D_Flip_Flop d_ff_9 (.D(multiplexer_1_out[8]), .clk(CLK), .Q(d_ff_1_q[8]), .reset(and_1_out));  // open: Qn, preset
  D_Flip_Flop d_ff_10 (.D(multiplexer_1_out[9]), .clk(CLK), .Q(d_ff_1_q[9]), .reset(and_1_out));  // open: Qn, preset
  D_Flip_Flop d_ff_11 (.D(multiplexer_1_out[10]), .clk(CLK), .Q(d_ff_1_q[10]), .reset(and_1_out));  // open: Qn, preset
  D_Flip_Flop d_ff_12 (.D(multiplexer_1_out[11]), .clk(CLK), .Q(d_ff_1_q[11]), .reset(and_1_out));  // open: Qn, preset
  D_Flip_Flop d_ff_13 (.D(multiplexer_1_out[12]), .clk(CLK), .Q(d_ff_1_q[12]), .reset(and_1_out));  // open: Qn, preset
  D_Flip_Flop d_ff_14 (.D(multiplexer_1_out[13]), .clk(CLK), .Q(d_ff_1_q[13]), .reset(and_1_out));  // open: Qn, preset
  D_Flip_Flop d_ff_15 (.D(multiplexer_1_out[14]), .clk(CLK), .Q(d_ff_1_q[14]), .reset(and_1_out));  // open: Qn, preset
  D_Flip_Flop d_ff_16 (.D(multiplexer_1_out[15]), .clk(CLK), .Q(d_ff_1_q[15]), .reset(and_1_out));  // open: Qn, preset
  Adder #(.width(16)) adder_1 (.a(d_ff_1_q), .b({16{1'b0}}), .out(adder_1_out), .cin(1'b1));  // open: cout
  Multiplexer #(.width(16)) multiplexer_2 (.in0(d_ff_1_q), .in1(adder_1_out), .out(O), .sel(INC));

  // Other names for the same wires on the sheet: INC_16BIT = INC; INCo_16BIT[15:0] = O; LD_16BIT = LD
endmodule

module REGISTER12BIT (
  input  LD,
  input  INC,
  input  CLR,
  input  CLK,
  input  [15:0] D,
  output [15:0] O
);

  wire and_1_out, not_1_out, SL1_12BIT;
  wire [11:0] adder_1_out, d_ff_1_q, multiplexer_1_out;

  Multiplexer #(.width(12)) multiplexer_1 (.in0(O[11:0]), .in1(D[11:0]), .out(multiplexer_1_out), .sel(LD));
  and and_1 (and_1_out, CLR, CLK);
  not not_1 (not_1_out, LD);
  and and_2 (SL1_12BIT, not_1_out, INC);
  D_Flip_Flop d_ff_1 (.D(multiplexer_1_out[0]), .clk(CLK), .Q(d_ff_1_q[0]), .reset(and_1_out));  // open: Qn, preset
  D_Flip_Flop d_ff_2 (.D(multiplexer_1_out[1]), .clk(CLK), .Q(d_ff_1_q[1]), .reset(and_1_out));  // open: Qn, preset
  D_Flip_Flop d_ff_3 (.D(multiplexer_1_out[2]), .clk(CLK), .Q(d_ff_1_q[2]), .reset(and_1_out));  // open: Qn, preset
  D_Flip_Flop d_ff_4 (.D(multiplexer_1_out[3]), .clk(CLK), .Q(d_ff_1_q[3]), .reset(and_1_out));  // open: Qn, preset
  D_Flip_Flop d_ff_5 (.D(multiplexer_1_out[4]), .clk(CLK), .Q(d_ff_1_q[4]), .reset(and_1_out));  // open: Qn, preset
  D_Flip_Flop d_ff_6 (.D(multiplexer_1_out[5]), .clk(CLK), .Q(d_ff_1_q[5]), .reset(and_1_out));  // open: Qn, preset
  D_Flip_Flop d_ff_7 (.D(multiplexer_1_out[6]), .clk(CLK), .Q(d_ff_1_q[6]), .reset(and_1_out));  // open: Qn, preset
  D_Flip_Flop d_ff_8 (.D(multiplexer_1_out[7]), .clk(CLK), .Q(d_ff_1_q[7]), .reset(and_1_out));  // open: Qn, preset
  D_Flip_Flop d_ff_9 (.D(multiplexer_1_out[8]), .clk(CLK), .Q(d_ff_1_q[8]), .reset(and_1_out));  // open: Qn, preset
  D_Flip_Flop d_ff_10 (.D(multiplexer_1_out[9]), .clk(CLK), .Q(d_ff_1_q[9]), .reset(and_1_out));  // open: Qn, preset
  D_Flip_Flop d_ff_11 (.D(multiplexer_1_out[10]), .clk(CLK), .Q(d_ff_1_q[10]), .reset(and_1_out));  // open: Qn, preset
  D_Flip_Flop d_ff_12 (.D(multiplexer_1_out[11]), .clk(CLK), .Q(d_ff_1_q[11]), .reset(and_1_out));  // open: Qn, preset
  Adder #(.width(12)) adder_1 (.a(d_ff_1_q), .b({12{1'b0}}), .out(adder_1_out), .cin(1'b1));  // open: cout
  Multiplexer #(.width(12)) multiplexer_2 (.in0(d_ff_1_q), .in1(adder_1_out), .out(O[11:0]), .sel(INC));

  assign O[15:12] = 4'b0000;

  // Other names for the same wires on the sheet: INC_12BIT = INC; LD_12BIT = LD; INCo_12BIT[11:0] = O[11:0]
endmodule

module ALU (
  input  [15:0] AC,
  input  [15:0] DR,
  input  [7:0] INPR,
  input  [3:0] Timer,
  input  [15:0] IR,
  input  E,
  output [15:0] ALU_OUTPUT,
  output ExtendBit
);

  wire adder_1_cout, and_2_out, and_3_out, and_4_out, and_5_out, and_6_out, and_7_out, and_8_out, and_9_out,
       and_10_out, and_11_out, decoder_1_out3, decoder_1_out5, decoder_2_out0, decoder_2_out1,
       decoder_2_out2, decoder_2_out7, multiplexer_1_out, not_2_out, not_3_out, not_4_out, or_1_out;
  wire [2:0] ALU_DECIDER;
  wire [15:0] adder_1_out, and_1_out, not_1_out, shifter_1_out, shifter_2_out;

  Shifter #(.shift("lr"), .width(16)) shifter_1 (.in(AC), .\dist (4'b0001), .out(shifter_1_out));
  Shifter #(.width(16)) shifter_2 (.in(AC), .\dist (4'b0001), .out(shifter_2_out));
  assign and_1_out = AC & DR;  // AND_Gate and_1, 16 bits wide
  Adder #(.width(16)) adder_1 (.a(AC), .b(DR), .out(adder_1_out), .cout(adder_1_cout));  // open: cin
  assign not_1_out = ~AC;  // NOT_Gate not_1, 16 bits wide
  Multiplexer #(.select(3)) multiplexer_1 (
    .in0(E), .in1(E), .in2(adder_1_cout), .in3(E), .in4(E), .in5(E), .in6(AC[15]), .in7(AC[0]),
    .out(multiplexer_1_out), .sel(ALU_DECIDER));
  not not_2 (not_2_out, E);
  Multiplexer #(.select(3), .width(16)) multiplexer_2 (
    .in0(AC), .in1(and_1_out), .in2(adder_1_out), .in3(DR), .in4({{8{1'b1}}, INPR}), .in5(not_1_out),
    .in6({E, shifter_1_out[14:0]}), .in7({shifter_2_out[15:1], E}), .out(ALU_OUTPUT), .sel(ALU_DECIDER));
  and and_2 (and_2_out, IR[8], and_4_out);
  Multiplexer multiplexer_3 (.in0(multiplexer_1_out), .in1(not_2_out), .out(ExtendBit), .sel(and_2_out));
  not not_3 (not_3_out, IR[15]);
  Decoder #(.enable("false"), .select(4)) decoder_1 (
    .out3(decoder_1_out3), .out5(decoder_1_out5), .sel(Timer));  // open: out0, out1, out2, out4, out6, out7, out8, out9, out10, out11, out12, out13, out14, out15
  Decoder #(.enable("false"), .select(3)) decoder_2 (
    .out0(decoder_2_out0), .out1(decoder_2_out1), .out2(decoder_2_out2), .out7(decoder_2_out7),
    .sel(IR[14:12]));  // open: out3, out4, out5, out6
  and and_3 (and_3_out, IR[15], decoder_2_out7, decoder_1_out3);
  and and_4 (and_4_out, not_3_out, decoder_2_out7, decoder_1_out3);
  and and_5 (and_5_out, decoder_2_out0, decoder_1_out5);
  and and_6 (and_6_out, decoder_2_out1, decoder_1_out5);
  and and_7 (and_7_out, decoder_2_out2, decoder_1_out5);
  and and_8 (and_8_out, and_3_out, IR[11]);
  and and_9 (and_9_out, and_4_out, IR[6]);
  and and_10 (and_10_out, and_4_out, IR[7]);
  and and_11 (and_11_out, and_4_out, IR[9]);
  or or_1 (or_1_out, and_5_out, and_6_out, and_7_out, and_8_out, and_9_out, and_10_out, and_11_out);
  not not_4 (not_4_out, or_1_out);
  Priority_Encoder priority_encoder_1 (
    .in0(not_4_out), .in1(and_5_out), .in2(and_6_out), .in3(and_7_out), .in4(and_8_out), .in5(and_9_out),
    .in6(and_10_out), .in7(and_11_out), .out(ALU_DECIDER));  // open: en_in, gs, en_out

  // Other names for the same wires on the sheet: ALU_AC[15:0] = AC; ALU_DR[15:0] = DR; ALU_INPR[7:0] = INPR;
  //   ALU_INPR_16BIT[7:0] = INPR
endmodule

module OUTR (
  input  CLK,
  input  CLR,
  input  LD,
  input  [15:0] D,
  output [7:0] O
);

  wire and_1_out, and_2_out;

  and and_1 (and_1_out, CLK, CLR);
  and and_2 (and_2_out, CLK, LD);
  D_Flip_Flop d_ff_1 (.D(D[0]), .clk(and_2_out), .Q(O[0]), .reset(and_1_out));  // open: Qn, preset
  D_Flip_Flop d_ff_2 (.D(D[1]), .clk(and_2_out), .Q(O[1]), .reset(and_1_out));  // open: Qn, preset
  D_Flip_Flop d_ff_3 (.D(D[2]), .clk(and_2_out), .Q(O[2]), .reset(and_1_out));  // open: Qn, preset
  D_Flip_Flop d_ff_4 (.D(D[3]), .clk(and_2_out), .Q(O[3]), .reset(and_1_out));  // open: Qn, preset
  D_Flip_Flop d_ff_5 (.D(D[4]), .clk(and_2_out), .Q(O[4]), .reset(and_1_out));  // open: Qn, preset
  D_Flip_Flop d_ff_6 (.D(D[5]), .clk(and_2_out), .Q(O[5]), .reset(and_1_out));  // open: Qn, preset
  D_Flip_Flop d_ff_7 (.D(D[6]), .clk(and_2_out), .Q(O[6]), .reset(and_1_out));  // open: Qn, preset
  D_Flip_Flop d_ff_8 (.D(D[7]), .clk(and_2_out), .Q(O[7]), .reset(and_1_out));  // open: Qn, preset
endmodule

module INPR (
  input  [7:0] D,
  output [7:0] O
);


  assign O = D;
endmodule

module COUNTER4BIT (
  input  INR,
  input  CLK,
  input  CLR,
  output [3:0] O
);

  wire and_1_out, and_2_out, d_ff_1_qn, d_ff_2_qn, d_ff_3_qn, d_ff_4_qn;

  and and_1 (and_1_out, INR, CLK);
  and and_2 (and_2_out, CLK, CLR);
  D_Flip_Flop d_ff_1 (.D(d_ff_1_qn), .clk(and_1_out), .Q(O[0]), .Qn(d_ff_1_qn), .reset(and_2_out));  // open: preset
  D_Flip_Flop d_ff_2 (.D(d_ff_2_qn), .clk(d_ff_1_qn), .Q(O[1]), .Qn(d_ff_2_qn), .reset(and_2_out));  // open: preset
  D_Flip_Flop d_ff_3 (.D(d_ff_3_qn), .clk(d_ff_2_qn), .Q(O[2]), .Qn(d_ff_3_qn), .reset(and_2_out));  // open: preset
  D_Flip_Flop d_ff_4 (.D(d_ff_4_qn), .clk(d_ff_3_qn), .Q(O[3]), .Qn(d_ff_4_qn), .reset(and_2_out));  // open: preset
endmodule

module AR_CONTROLLER (
  input  [15:0] IR,
  input  [3:0] Timer,
  input  R,
  output AR_LD,
  output AR_INR,
  output AR_CLR
);

  wire and_1_out, and_2_out, decoder_1_out0, decoder_1_out2, decoder_1_out3, decoder_1_out4, decoder_2_out5,
       decoder_2_out7, not_1_out, not_2_out, or_1_out;

  Decoder #(.enable("false"), .select(4)) decoder_1 (
    .out0(decoder_1_out0), .out2(decoder_1_out2), .out3(decoder_1_out3), .out4(decoder_1_out4), .sel(Timer));  // open: out1, out5, out6, out7, out8, out9, out10, out11, out12, out13, out14, out15
  not not_1 (not_1_out, R);
  Decoder #(.enable("false"), .select(3)) decoder_2 (
    .out5(decoder_2_out5), .out7(decoder_2_out7), .sel(IR[14:12]));  // open: out0, out1, out2, out3, out4, out6
  not not_2 (not_2_out, decoder_2_out7);
  or or_1 (or_1_out, decoder_1_out0, decoder_1_out2);
  and and_1 (and_1_out, or_1_out, not_1_out);
  and and_2 (and_2_out, not_2_out, IR[15], decoder_1_out3);
  and and_3 (AR_INR, decoder_2_out5, decoder_1_out4);
  and and_4 (AR_CLR, decoder_1_out0, R);
  or or_2 (AR_LD, and_1_out, and_2_out);
endmodule

module DR_CONTROLLER (
  input  [15:0] IR,
  input  [3:0] Timer,
  output DR_LD,
  output DR_INR
);

  wire decoder_1_out4, decoder_1_out5, decoder_2_out0, decoder_2_out1, decoder_2_out2, decoder_2_out6,
       or_1_out;

  Decoder #(.enable("false"), .select(4)) decoder_1 (
    .out4(decoder_1_out4), .out5(decoder_1_out5), .sel(Timer));  // open: out0, out1, out2, out3, out6, out7, out8, out9, out10, out11, out12, out13, out14, out15
  Decoder #(.enable("false"), .select(3)) decoder_2 (
    .out0(decoder_2_out0), .out1(decoder_2_out1), .out2(decoder_2_out2), .out6(decoder_2_out6),
    .sel(IR[14:12]));  // open: out3, out4, out5, out7
  or or_1 (or_1_out, decoder_2_out0, decoder_2_out1, decoder_2_out2, decoder_2_out6);
  and and_1 (DR_LD, or_1_out, decoder_1_out4);
  and and_2 (DR_INR, decoder_2_out6, decoder_1_out5);
endmodule

module TR_CONTROLLER (
  input  R,
  input  [3:0] Timer,
  output TR_LD
);

  wire decoder_1_out0;

  Decoder #(.enable("false"), .select(4)) decoder_1 (
    .out0(decoder_1_out0), .sel(Timer));  // open: out1, out2, out3, out4, out5, out6, out7, out8, out9, out10, out11, out12, out13, out14, out15
  and and_1 (TR_LD, decoder_1_out0, R);
endmodule

module OUTR_CONTROLLER (
  input  [15:0] IR,
  input  [3:0] Timer,
  output OUTR_LD
);

  wire and_1_out, decoder_1_out3, decoder_2_out7;

  Decoder #(.enable("false"), .select(4)) decoder_1 (
    .out3(decoder_1_out3), .sel(Timer));  // open: out0, out1, out2, out4, out5, out6, out7, out8, out9, out10, out11, out12, out13, out14, out15
  Decoder #(.enable("false"), .select(3)) decoder_2 (
    .out7(decoder_2_out7), .sel(IR[14:12]));  // open: out0, out1, out2, out3, out4, out5, out6
  and and_1 (and_1_out, decoder_2_out7, decoder_1_out3, IR[15]);
  and and_2 (OUTR_LD, IR[10], and_1_out);
endmodule

module IR_CONTROLLER (
  input  R,
  input  [3:0] Timer,
  output IR_LD
);

  wire decoder_1_out1, not_1_out;

  Decoder #(.enable("false"), .select(4)) decoder_1 (
    .out1(decoder_1_out1), .sel(Timer));  // open: out0, out2, out3, out4, out5, out6, out7, out8, out9, out10, out11, out12, out13, out14, out15
  not not_1 (not_1_out, R);
  and and_1 (IR_LD, decoder_1_out1, not_1_out);
endmodule

module PC_CONTROLLER (
  input  [15:0] IR,
  input  [3:0] Timer,
  input  R,
  input  [15:0] DR,
  input  [15:0] AC,
  input  E,
  input  FGI,
  input  FGO,
  output PC_LD,
  output PC_CLR,
  output PC_INR
);

  wire and_1_out, and_2_out, and_3_out, and_4_out, and_5_out, and_6_out, and_7_out, and_8_out, and_9_out,
       and_10_out, and_11_out, and_12_out, and_13_out, and_14_out, and_15_out, decoder_1_out1,
       decoder_1_out2, decoder_1_out4, decoder_1_out5, decoder_1_out6, decoder_2_out4, decoder_2_out5,
       decoder_2_out6, decoder_2_out7, nor_1_out, nor_2_out, nor_3_out, not_1_out, not_2_out, not_3_out,
       not_4_out, or_1_out, or_2_out;

  nor nor_1 (nor_1_out, DR[0], DR[1], DR[2], DR[3], DR[4], DR[5], DR[7], DR[6], DR[8], DR[9], DR[10], DR[11], DR[12], DR[13], DR[14], DR[15]);
  nor nor_2 (nor_2_out, AC[0], AC[1], AC[2], AC[3], AC[4], AC[5], AC[7], AC[6], AC[8], AC[9], AC[10], AC[11], AC[12], AC[13], AC[14], AC[15]);
  nor nor_3 (nor_3_out, AC[15], AC[15]);
  not not_1 (not_1_out, E);
  Decoder #(.enable("false"), .select(4)) decoder_1 (
    .out1(decoder_1_out1), .out2(decoder_1_out2), .out4(decoder_1_out4), .out5(decoder_1_out5),
    .out6(decoder_1_out6), .sel(Timer));  // open: out0, out3, out7, out8, out9, out10, out11, out12, out13, out14, out15
  not not_2 (not_2_out, R);
  not not_3 (not_3_out, nor_3_out);
  Decoder #(.enable("false"), .select(3)) decoder_2 (
    .out4(decoder_2_out4), .out5(decoder_2_out5), .out6(decoder_2_out6), .out7(decoder_2_out7),
    .sel(IR[14:12]));  // open: out0, out1, out2, out3
  not not_4 (not_4_out, IR[15]);
  and and_1 (and_1_out, IR[4], not_3_out);
  and and_2 (and_2_out, IR[3], nor_3_out);
  and and_3 (and_3_out, IR[2], nor_2_out);
  and and_4 (and_4_out, IR[1], not_1_out);
  and and_5 (and_5_out, FGI, IR[9]);
  and and_6 (and_6_out, FGO, IR[8]);
  and and_7 (and_7_out, decoder_2_out7, not_4_out, decoder_1_out4);
  and and_8 (and_8_out, decoder_2_out7, IR[15], decoder_1_out4);
  and and_9 (and_9_out, decoder_1_out1, not_2_out);
  and and_10 (and_10_out, R, decoder_1_out2);
  and and_11 (and_11_out, decoder_2_out6, decoder_1_out6, nor_1_out);
  or or_1 (or_1_out, and_1_out, and_2_out, and_3_out, and_4_out);
  or or_2 (or_2_out, and_5_out, and_6_out);
  and and_12 (and_12_out, and_7_out, or_1_out);
  and and_13 (and_13_out, and_8_out, or_2_out);
  and and_14 (and_14_out, decoder_2_out4, decoder_1_out4);
  and and_15 (and_15_out, decoder_2_out5, decoder_1_out5);
  or or_3 (PC_LD, and_14_out, and_15_out);
  or or_4 (PC_INR, and_9_out, and_10_out, and_11_out, and_12_out, and_13_out);
  and and_16 (PC_CLR, decoder_1_out1, R);
endmodule

module AC_CONTROLLER (
  input  [15:0] IR,
  input  [3:0] Timer,
  output AC_INR,
  output AC_CLR,
  output AC_LD
);

  wire and_1_out, and_2_out, and_5_out, and_6_out, and_7_out, decoder_1_out3, decoder_1_out5, decoder_2_out0,
       decoder_2_out1, decoder_2_out2, decoder_2_out7, not_1_out, or_1_out, or_2_out;

  Decoder #(.enable("false"), .select(4)) decoder_1 (
    .out3(decoder_1_out3), .out5(decoder_1_out5), .sel(Timer));  // open: out0, out1, out2, out4, out6, out7, out8, out9, out10, out11, out12, out13, out14, out15
  or or_1 (or_1_out, IR[9], IR[7], IR[6]);
  Decoder #(.enable("false"), .select(3)) decoder_2 (
    .out0(decoder_2_out0), .out1(decoder_2_out1), .out2(decoder_2_out2), .out7(decoder_2_out7),
    .sel(IR[14:12]));  // open: out3, out4, out5, out6
  not not_1 (not_1_out, IR[15]);
  or or_2 (or_2_out, decoder_2_out0, decoder_2_out1, decoder_2_out2);
  and and_1 (and_1_out, decoder_2_out7, not_1_out, decoder_1_out3);
  and and_2 (and_2_out, decoder_2_out7, IR[15], decoder_1_out3);
  and and_3 (AC_INR, and_1_out, IR[5]);
  and and_4 (AC_CLR, and_1_out, IR[11]);
  and and_5 (and_5_out, IR[11], and_2_out);
  and and_6 (and_6_out, and_1_out, or_1_out);
  and and_7 (and_7_out, or_2_out, decoder_1_out5);
  or or_3 (AC_LD, and_5_out, and_6_out, and_7_out);
endmodule

module BUS_CONTROLLER (
  input  [15:0] IR,
  input  [3:0] Timer,
  input  R,
  output x1,
  output x2,
  output x3,
  output x4,
  output x5,
  output x6,
  output x7
);

  wire and_1_out, and_2_out, and_3_out, and_4_out, and_5_out, and_6_out, and_7_out, and_8_out, and_9_out,
       decoder_1_out0, decoder_1_out1, decoder_1_out2, decoder_1_out3, decoder_1_out4, decoder_1_out5,
       decoder_1_out6, decoder_1_out7, decoder_2_out0, decoder_2_out1, decoder_2_out2, decoder_2_out3,
       decoder_2_out4, decoder_2_out5, decoder_2_out6, not_1_out, not_2_out, or_1_out, or_2_out;

  Decoder #(.enable("false"), .select(3)) decoder_1 (
    .out0(decoder_1_out0), .out1(decoder_1_out1), .out2(decoder_1_out2), .out3(decoder_1_out3),
    .out4(decoder_1_out4), .out5(decoder_1_out5), .out6(decoder_1_out6), .out7(decoder_1_out7),
    .sel(IR[14:12]));
  Decoder #(.enable("false"), .select(4)) decoder_2 (
    .out0(decoder_2_out0), .out1(decoder_2_out1), .out2(decoder_2_out2), .out3(decoder_2_out3),
    .out4(decoder_2_out4), .out5(decoder_2_out5), .out6(decoder_2_out6), .sel(Timer));  // open: out7, out8, out9, out10, out11, out12, out13, out14, out15
  not not_1 (not_1_out, R);
  not not_2 (not_2_out, decoder_1_out7);
  or or_1 (or_1_out, not_1_out, R);
  or or_2 (or_2_out, decoder_1_out0, decoder_1_out1, decoder_1_out2, decoder_1_out6);
  and and_1 (and_1_out, decoder_2_out1, not_1_out);
  and and_2 (and_2_out, not_2_out, IR[15], decoder_2_out3);
  and and_3 (and_3_out, decoder_2_out4, or_2_out);
  and and_4 (and_4_out, decoder_1_out4, decoder_2_out4);
  and and_5 (and_5_out, decoder_1_out5, decoder_2_out5);
  and and_6 (and_6_out, decoder_1_out5, decoder_2_out4);
  and and_7 (and_7_out, or_1_out, decoder_2_out0);
  and and_8 (and_8_out, decoder_1_out2, decoder_2_out5);
  and and_9 (and_9_out, decoder_1_out6, decoder_2_out6);
  or or_3 (x1, and_4_out, and_5_out);
  or or_4 (x2, and_6_out, and_7_out);
  or or_5 (x3, and_8_out, and_9_out);
  and and_10 (x4, decoder_1_out3, decoder_2_out4);
  and and_11 (x5, not_1_out, decoder_2_out2);
  and and_12 (x6, R, decoder_2_out1);
  or or_6 (x7, and_1_out, and_2_out, and_3_out);
endmodule

module BUS_8x3_ENCODER (
  input  x1,
  input  x2,
  input  x3,
  input  x4,
  input  x5,
  input  x6,
  input  x7,
  output S0,
  output S1,
  output S2
);

  or or_1 (S0, x1, x3, x5, x7);
  or or_2 (S1, x2, x3, x6, x7);
  or or_3 (S2, x4, x5, x6, x7);
endmodule

module RAM_CONTROLLER (
  input  [15:0] IR,
  input  [3:0] Timer,
  input  R,
  output Read,
  output Write
);

  wire and_1_out, and_2_out, and_3_out, and_4_out, and_5_out, and_6_out, and_7_out, decoder_1_out0,
       decoder_1_out1, decoder_1_out2, decoder_1_out3, decoder_1_out5, decoder_1_out6, decoder_1_out7,
       decoder_2_out1, decoder_2_out3, decoder_2_out4, decoder_2_out6, not_1_out, not_2_out, or_2_out;

  Decoder #(.enable("false"), .select(3)) decoder_1 (
    .out0(decoder_1_out0), .out1(decoder_1_out1), .out2(decoder_1_out2), .out3(decoder_1_out3),
    .out5(decoder_1_out5), .out6(decoder_1_out6), .out7(decoder_1_out7), .sel(IR[14:12]));  // open: out4
  Decoder #(.enable("false"), .select(4)) decoder_2 (
    .out1(decoder_2_out1), .out3(decoder_2_out3), .out4(decoder_2_out4), .out6(decoder_2_out6), .sel(Timer));  // open: out0, out2, out5, out7, out8, out9, out10, out11, out12, out13, out14, out15
  and and_1 (and_1_out, R, decoder_2_out1);
  and and_2 (and_2_out, decoder_1_out3, decoder_2_out4);
  and and_3 (and_3_out, decoder_1_out5, decoder_2_out4);
  and and_4 (and_4_out, decoder_1_out6, decoder_2_out6);
  not not_1 (not_1_out, decoder_1_out7);
  and and_5 (and_5_out, decoder_2_out1, not_2_out);
  not not_2 (not_2_out, R);
  or or_1 (Write, and_1_out, and_2_out, and_3_out, and_4_out);
  and and_6 (and_6_out, not_1_out, IR[15], decoder_2_out3);
  or or_2 (or_2_out, decoder_1_out0, decoder_1_out1, decoder_1_out2, decoder_1_out6);
  and and_7 (and_7_out, or_2_out, decoder_2_out4);
  or or_3 (Read, and_7_out, and_6_out, and_5_out);
endmodule

module FF_CONTROLLER (
  input  alu_E,
  input  START,
  input  [15:0] IR,
  input  [3:0] Timer,
  input  R,
  input  IEN,
  input  FGI,
  input  FGO,
  input  CLK,
  output Eset,
  output Eclr,
  output Iset,
  output Sset,
  output Sclr,
  output Rset,
  output Rclr,
  output IENset,
  output IENclr,
  output FGIclr,
  output FGOclr,
  output CLKI,
  output CLKS,
  output CLKR,
  output CLKIEN,
  output CLKFGI,
  output CLKFGO,
  output CLKE
);

  wire and_3_out, and_4_out, and_9_out, decoder_1_out7, decoder_2_out0, decoder_2_out1, decoder_2_out2,
       decoder_2_out3, not_1_out, not_2_out, not_3_out, not_4_out, not_5_out, or_1_out;

  Decoder #(.enable("false"), .select(3)) decoder_1 (
    .out7(decoder_1_out7), .sel(IR[14:12]));  // open: out0, out1, out2, out3, out4, out5, out6
  not not_1 (not_1_out, IR[15]);
  Decoder #(.enable("false"), .select(4)) decoder_2 (
    .out0(decoder_2_out0), .out1(decoder_2_out1), .out2(decoder_2_out2), .out3(decoder_2_out3), .sel(Timer));  // open: out4, out5, out6, out7, out8, out9, out10, out11, out12, out13, out14, out15
  not not_2 (not_2_out, R);
  or or_1 (or_1_out, FGI, FGO);
  and and_1 (Iset, decoder_2_out2, not_2_out);
  and and_2 (Rclr, R, decoder_2_out2);
  and and_3 (and_3_out, decoder_1_out7, not_1_out, decoder_2_out3);
  and and_4 (and_4_out, decoder_1_out7, IR[15], decoder_2_out3);
  and and_5 (FGIclr, IR[11], and_4_out);
  and and_6 (FGOclr, IR[10], and_4_out);
  not not_3 (not_3_out, decoder_2_out0);
  not not_4 (not_4_out, decoder_2_out1);
  and and_7 (Rset, not_3_out, not_4_out, not_5_out, IEN, or_1_out);
  not not_5 (not_5_out, decoder_2_out2);
  and and_8 (Sclr, and_3_out, IR[0]);
  and and_9 (and_9_out, IR[6], and_4_out);
  and and_10 (IENset, IR[7], and_4_out);
  and and_11 (Eclr, IR[10], and_3_out);
  and and_12 (IENclr, Rclr, and_9_out);

  assign CLKE = CLK;
  assign CLKFGI = CLK;
  assign CLKFGO = CLK;
  assign CLKI = CLK;
  assign CLKIEN = CLK;
  assign CLKR = CLK;
  assign CLKS = CLK;
  assign Eset = alu_E;
  assign Sset = START;
endmodule

module RAM_ADJUSTER (
  input  [15:0] RAM_INPUT_IN,
  output [11:0] RAM_OUTPUT_OUT
);


  assign RAM_OUTPUT_OUT = RAM_INPUT_IN[11:0];
endmodule

module SC_CONTROLLER_CLR (
  input  [15:0] IR,
  input  [3:0] Timer,
  input  R,
  output SC_CLR_OUT
);

  wire and_1_out, and_2_out, and_3_out, and_4_out, and_5_out, and_6_out, and_7_out, and_8_out, and_9_out,
       and_10_out, decoder_1_out0, decoder_1_out1, decoder_1_out2, decoder_1_out3, decoder_1_out4,
       decoder_1_out5, decoder_1_out6, decoder_1_out7, decoder_2_out3, decoder_2_out4, decoder_2_out5,
       decoder_2_out6, decoder_2_out7, not_1_out, not_2_out;

  Decoder #(.enable("false"), .select(3)) decoder_1 (
    .out0(decoder_1_out0), .out1(decoder_1_out1), .out2(decoder_1_out2), .out3(decoder_1_out3),
    .out4(decoder_1_out4), .out5(decoder_1_out5), .out6(decoder_1_out6), .out7(decoder_1_out7),
    .sel(IR[14:12]));
  not not_1 (not_1_out, IR[15]);
  Decoder #(.enable("false"), .select(4)) decoder_2 (
    .out3(decoder_2_out3), .out4(decoder_2_out4), .out5(decoder_2_out5), .out6(decoder_2_out6),
    .out7(decoder_2_out7), .sel(Timer));  // open: out0, out1, out2, out8, out9, out10, out11, out12, out13, out14, out15
  not not_2 (not_2_out, R);
  and and_1 (and_1_out, decoder_2_out3, R);
  and and_2 (and_2_out, decoder_1_out7, not_1_out, decoder_2_out4);
  and and_3 (and_3_out, decoder_1_out7, IR[15], decoder_2_out4);
  and and_4 (and_4_out, decoder_2_out7, decoder_1_out6);
  and and_5 (and_5_out, decoder_1_out5, decoder_2_out6);
  and and_6 (and_6_out, decoder_1_out4, decoder_2_out5);
  and and_7 (and_7_out, decoder_1_out3, decoder_2_out5);
  and and_8 (and_8_out, decoder_1_out2, decoder_2_out6);
  and and_9 (and_9_out, decoder_1_out1, decoder_2_out6);
  and and_10 (and_10_out, decoder_1_out0, decoder_2_out6);
  or or_1 (SC_CLR_OUT, and_2_out, and_3_out, and_4_out, and_5_out, and_6_out, and_7_out, and_8_out, and_9_out, and_10_out, and_1_out);
endmodule
